// Logisim project FLOATING_POINT_ADDER.circ as structural Verilog: 32 circuits, main circuit main
module main (
  input  [31:0] A,
  input  [31:0] B,
  output [31:0] A___B,
  output Float,
  output INF,
  output NaN,
  output De_Norm,
  output Zero,
  output Underflow,
  output Overflow
);

  FPA fpa_1 (
    .A(A), .B(B), .Y(A___B), .Overflow(Overflow), .Underflow(Underflow), .De_Normal(De_Norm),
    .Not_a_Number(NaN), .Infinity(INF), .Float(Float), .Zero(Zero));
endmodule

module TEST (
  input  S_A,
  input  [8:0] EXP_A,
  input  [21:0] FRACTION_A,
  input  S_B,
  input  [8:0] EXP_B,
  input  [21:0] FRACTION_B,
  output S_Y,
  output [8:0] EXP_Y,
  output [21:0] FRACTION_Y,
  output Float,
  output Zero,
  output INF,
  output NaN,
  output De_Norm,
  output Underflow,
  output Overflow
);

  LED led_1 (.in(S_A));
  LED led_2 (.in(S_B));
  // Probe on FRACTION_A
  // Probe on FRACTION_B
  // Probe on EXP_A
  // Probe on EXP_B
  // Probe on {S_A, EXP_A, FRACTION_A}
  // Probe on {S_B, EXP_B, FRACTION_B}
  FPA fpa_1 (
    .A({S_A, EXP_A, FRACTION_A}), .B({S_B, EXP_B, FRACTION_B}), .Y({S_Y, EXP_Y, FRACTION_Y}),
    .Overflow(Overflow), .Underflow(Underflow), .De_Normal(De_Norm), .Not_a_Number(NaN), .Infinity(INF),
    .Float(Float), .Zero(Zero));
  LED led_3 (.in(S_Y));
  // Probe on FRACTION_Y
  // Probe on EXP_Y
  // Probe on {S_Y, EXP_Y, FRACTION_Y}

  // Notes on the sheet:
  //   1.
  //   1.
  //   X 2 ^ 
  //   X 2 ^ 
  //   1.
  //   X 2 ^ 
endmodule

module FPA (
  input  [31:0] A,
  input  [31:0] B,
  output Overflow,
  output Underflow,
  output [31:0] Y,
  output Zero,
  output De_Normal,
  output Infinity,
  output Not_a_Number,
  output Float
);

  wire A_zero, and_1_out, B_zero, Larger_float_not_zero, NormalizationOverflow, not_2_out, or_1_out,
       RoundingOverflow, SameSign, Sign, zero_checker_2_iszero, zero_checker_4_iszero;
  wire [8:0] exponent_difference, larger_exponent, NormalExponent, RoundedExponent, smaller_exponent;
  wire [21:0] RoundedSignificand;
  wire [24:0] NormalSignificand;
  wire [25:0] padded_significand_2;
  wire [25:3] padded_significand_2_prime;
  wire [26:0] AddedSignificand, ASU_Input_1, ASU_Input_2;
  wire [27:0] ASUOutput;
  wire [31:0] bit_extender_1_out, bit_extender_2_out, bit_extender_3_out, bit_extender_4_out,
       larger_exponent_float, n32_bit_mux_2_out, n32_bit_mux_3_out;
  wire [31:31] smaller_exponent_float;

  and and_1 (and_1_out, A_zero, B_zero);
  _32_bit_MUX u_32_bit_mux_1 (.A({Sign, RoundedExponent, RoundedSignificand}), .B({32{1'b0}}), .Out(Y), .S(and_1_out));
  Zero_Checker zero_checker_1 (.A(A), .IsZero(A_zero), .IgnoreSignBit(1'b1));
  not not_1 (Larger_float_not_zero, zero_checker_2_iszero);
  Zero_Checker zero_checker_2 (
    .A({larger_exponent_float[31], larger_exponent, larger_exponent_float[21:0]}),
    .IsZero(zero_checker_2_iszero), .IgnoreSignBit(1'b1));
  Subtractor #(.width(9)) subtractor_1 (
    .a(larger_exponent), .b(smaller_exponent), .out(exponent_difference), .bin(1'b0));  // open: bout
  ASU asu_1 (.B_Cin(1'b0), .A(ASU_Input_1), .B(ASU_Input_2), .Y(ASUOutput), .Add(SameSign));
  NORMALISER normaliser_1 (
    .S(AddedSignificand), .Normal_Significand(NormalSignificand), .Exponent(larger_exponent),
    .Normal_Exponent(NormalExponent), .Normalizing_Overflow(NormalizationOverflow), .Underflow(Underflow));
  xnor xnor_1 (SameSign, A[31], B[31]);
  ABS abs_1 (.A(ASUOutput), .ABS(AddedSignificand));
  REARRANGER rearranger_1 (
    .EXP_A(A[30:22]), .EXP_B(B[30:22]), .SIG_A(A), .SIG_B(B),
    .larger({larger_exponent_float[31], larger_exponent, larger_exponent_float[21:0]}),
    .smaller({smaller_exponent_float[31], smaller_exponent, padded_significand_2_prime[24:3]}));
  assign bit_extender_1_out = {{6{1'b0}}, {Larger_float_not_zero, larger_exponent_float[21:0], 3'b000}};  // Bit_Extender bit_extender_1
  assign bit_extender_2_out = {{6{1'b0}}, padded_significand_2};  // Bit_Extender bit_extender_2
  assign bit_extender_3_out = {{6{1'b0}}, {Larger_float_not_zero, larger_exponent_float[21:0], 3'b000}};  // Bit_Extender bit_extender_3
  assign bit_extender_4_out = {{6{1'b0}}, padded_significand_2};  // Bit_Extender bit_extender_4
  or or_1 (or_1_out, NormalizationOverflow, RoundingOverflow);
  _32_bit_MUX u_32_bit_mux_2 (
    .A(bit_extender_1_out), .B(bit_extender_2_out), .Out(n32_bit_mux_2_out), .S(larger_exponent_float[31]));
  _32_bit_MUX u_32_bit_mux_3 (
    .A(bit_extender_4_out), .B(bit_extender_3_out), .Out(n32_bit_mux_3_out), .S(larger_exponent_float[31]));
  not not_2 (not_2_out, Underflow);
  Zero_Checker zero_checker_3 (.A(B), .IsZero(B_zero), .IgnoreSignBit(1'b1));
  Bit_Extender #(.in_width(32), .out_width(27)) bit_extender_5 (.in(n32_bit_mux_2_out), .out(ASU_Input_1));
  Bit_Extender #(.in_width(32), .out_width(27)) bit_extender_6 (.in(n32_bit_mux_3_out), .out(ASU_Input_2));
  and and_2 (Overflow, or_1_out, not_2_out);
  Flags_Checker flags_checker_1 (
    .Fraction(RoundedSignificand), .Exponent(RoundedExponent), .ZERO(Zero), .DE_NORM(De_Normal),
    .INF(Infinity), .NaN(Not_a_Number), .Floating_Point_Number(Float));
  Zero_Checker zero_checker_4 (
    .A({smaller_exponent_float[31], smaller_exponent, padded_significand_2_prime[24:3]}),
    .IsZero(zero_checker_4_iszero), .IgnoreSignBit(1'b1));
  not not_3 (padded_significand_2_prime[25], zero_checker_4_iszero);
  RIGHT_SHIFT_WRAPPER right_shift_wrapper_1 (
    .A({padded_significand_2_prime, 3'b000}), .S(exponent_difference), .Y(padded_significand_2));
  Multiplexer #(.enable("false")) multiplexer_1 (.in0(ASUOutput[26]), .in1(A[31]), .out(Sign), .sel(SameSign));
  ROUNDER rounder_1 (
    .S(NormalSignificand), .Exponent(NormalExponent), .R(RoundedSignificand),
    .RoundedExponent(RoundedExponent), .RoundingOverflow(RoundingOverflow));

  // Other names for the same wires on the sheet: Significand_A[21:0] = A[21:0]; Exponent_A[8:0] = A[30:22];
  //   Sign_A = A[31]; SumSign = ASUOutput[26]; Significand_B[21:0] = B[21:0]; Exponent_B[8:0] = B[30:22];
  //   Sign_B = B[31]; larger_exponent_float[30:22] = larger_exponent; RearrangedSign1 = larger_exponent_float[31];
  //   padded_significand_1[25:3] = {Larger_float_not_zero, larger_exponent_float[21:0]};
  //   significand_of_larger_exp[21:0] = larger_exponent_float[21:0];
  //   significand_of_smaller_exp[21:0] = padded_significand_2_prime[24:3];
  //   smaller_exponent_float[30:0] = {smaller_exponent, padded_significand_2_prime[24:3]};
  //   Smaller_float_not_zero = padded_significand_2_prime[25]

  // Notes on the sheet:
  //   OUTPUT. If both input is zero we output zero.
  //   Again rearrange both numbers now based on sign of the larger float. Because larger negative number is always smaller.
  //   If A and B is same sign we add otherwise we subtract each other
  //   Normalises float. Can cause both overflow and underflow.
  //   Padding significant with GRS bits and implicit 1 (0 if the whole float is zero)   [ 1 bit + 22 bit + 3 bit ]
  //   Splitting the inputs into sign (1) , exponent (9) , significant (22)
  //   Rearranges both float by comparing their exponent
  //   Make both floats exponents equal. So take exp different and right shift the smaller floats significant.
  //   Both normaliser and rounder can cause overflow we take their OR value.
  //   Also overflow cannot occur if underflow bit is set
  //   Checks if A, B is zero or not (ignoring sign bit)
  //   Splitting the rearranged floats
  //   Check if any of the larger or smaller float is zero.
  //   Outputs all the flag of the generated output.
  //   Rounds the float using GRS bits. Adds 1 if G.(R + S + IN_0)
  //   If A and B signs are same we take the sign of the first number
  //   otherwise we take the sign of their subtraction result.
endmodule

module REARRANGER (
  input  [8:0] EXP_A,
  input  [8:0] EXP_B,
  input  [31:0] SIG_A,
  input  [31:0] SIG_B,
  output [31:0] larger,
  output [31:0] smaller
);

  wire b;

  Subtractor #(.width(9)) subtractor_1 (.a(EXP_A), .b(EXP_B), .bin(1'b0), .bout(b));  // open: out
  _32_bit_MUX u_32_bit_mux_1 (.A(SIG_A), .B(SIG_B), .Out(larger), .S(b));
  _32_bit_MUX u_32_bit_mux_2 (.A(SIG_B), .B(SIG_A), .Out(smaller), .S(b));
endmodule

module RIGHT_SHIFT_WRAPPER (
  input  [25:0] A,
  input  [8:0] S,
  output [25:0] Y
);

  wire [4:0] right_shift_adapter_1_e;
  wire [26:0] bit_extender_1_out;
  wire [26:26] right_shifter_1_y;

  // Probe on S
  // Probe on bit_extender_1_out
  assign bit_extender_1_out = {{1{1'b0}}, A};  // Bit_Extender bit_extender_1
  Right_Shift_Adapter right_shift_adapter_1 (.S(S), .E(right_shift_adapter_1_e));
  Right_Shifter right_shifter_1 (.A(bit_extender_1_out), .E(right_shift_adapter_1_e), .Y({right_shifter_1_y[26], Y}));
  // Probe on Y
endmodule

module NORMALISER (
  input  [26:0] S,
  input  [8:0] Exponent,
  output [24:0] Normal_Significand,
  output [8:0] Normal_Exponent,
  output Normalizing_Overflow,
  output Underflow
);

  wire Add, Carry, E0, E1, E2, E3, E4, E8, n7402_1_p1, n7432_1_p3, n7432_1_p6, n7432_1_p8, n7432_1_p9,
       n7432_3_p3, n7432_3_p6, Overflow_underflow, Sub;
  wire [4:0] LeftShiftAmount;
  wire [8:0] ModifiedExponent;
  wire [26:0] bit_extender_3_out, bit_extender_4_out, n1_bit_rs_1_out;
  wire [26:25] left_shifter_1_y;
  wire [27:10] asu_1_y;
  wire [31:0] bit_extender_1_out, bit_extender_2_out, n32_bit_mux_1_out;

  // _7432 7432_1: pin names not known; wires that end beside it: S[26], LeftShiftAmount[0], n7432_1_p3, n7432_1_p3, LeftShiftAmount[1], n7432_1_p6, LeftShiftAmount[2], n7432_1_p8, n7432_1_p9, LeftShiftAmount[3], n7432_1_p6, n7432_1_p8
  // _7432 7432_2: pin names not known; wires that end beside it: S[25], S[26], Add
  // _7404 7404_1: pin names not known; wires that end beside it: Add, Sub
  _1_bit_RS u_1_bit_rs_1 (.S(S), .Enable(S[26]), .out(n1_bit_rs_1_out));
  assign bit_extender_1_out = {{27{1'b0}}, LeftShiftAmount};  // Bit_Extender bit_extender_1
  assign bit_extender_2_out = {{31{1'b0}}, S[26]};  // Bit_Extender bit_extender_2
  // _7432 7432_3: pin names not known; wires that end beside it: LeftShiftAmount[4], n7432_1_p9, n7432_3_p3, n7432_3_p3, S[25], n7432_3_p6
  _32_bit_high_priority_encoder u_32_bit_high_priority_encoder_1 (
    ._1_based_indexing(1'b1), .In({S[24:0], {7{1'b0}}}), .EI(1'b0), .Out(LeftShiftAmount));
  Left_Shifter left_shifter_1 (
    .A(n1_bit_rs_1_out), .E({E4, E3, E2, E1, E0}), .Y({left_shifter_1_y, Normal_Significand}));
  // _7408 7408_1: pin names not known; wires that end beside it: n7432_3_p6, E8, Carry, Add, Overflow_underflow, Normalizing_Overflow, Overflow_underflow, Sub, Underflow
  _32_bit_MUX u_32_bit_mux_1 (.A(bit_extender_1_out), .B(bit_extender_2_out), .Out(n32_bit_mux_1_out), .S(Add));
  Bit_Extender #(.in_width(32), .out_width(27)) bit_extender_3 (.in(n32_bit_mux_1_out), .out(bit_extender_3_out));
  assign bit_extender_4_out = {{18{1'b0}}, Exponent};  // Bit_Extender bit_extender_4
  _9_bit_MUX u_9_bit_mux_1 (.A({9{1'b0}}), .B(ModifiedExponent), .S(n7432_3_p6), .Y(Normal_Exponent));
  // _7402 7402_1: pin names not known; wires that end beside it: n7402_1_p1, S[25], S[26]
  Error_Detector error_detector_1 (
    .Exponent(Normal_Exponent), .Carry_borrow(Carry), .Overflow_Underflow(Overflow_underflow));
  // _7408 7408_2: pin names not known; wires that end beside it: n7402_1_p1, LeftShiftAmount[4], E4, n7402_1_p1, LeftShiftAmount[3], E3, n7402_1_p1, LeftShiftAmount[2], E2, n7402_1_p1, LeftShiftAmount[1], E1
  ASU asu_1 (
    .B_Cin(1'b0), .A(bit_extender_4_out), .B(bit_extender_3_out), .Y({asu_1_y, E8, ModifiedExponent}),
    .Add(Add));
  // _7408 7408_3: pin names not known; wires that end beside it: n7402_1_p1, LeftShiftAmount[0], E0

  // Other names for the same wires on the sheet: O0 = LeftShiftAmount[0]; O1 = LeftShiftAmount[1];
  //   O2 = LeftShiftAmount[2]; O3 = LeftShiftAmount[3]; O4 = LeftShiftAmount[4]; Overflow = Normalizing_Overflow;
  //   S26 = S[25]; S27 = S[26]

  // Notes on the sheet:
  //   If 27th bit is set we right shift once
  //   to make the number normalised
  //   If there is not a single 1 in the significand then output 0
  //   (as implicit 1 also became 0)
  //   # If 27 and 26th bit was not set then we left shifted our significand 
  //   so now we have to subtract the amount of shift from our exp. (Add? = false)
  //   # If 27 or 26th bit was set then we right shifted or didnt shift (S27 = 0) our significand 
  //   so now we have to add S27 (we right shifted once if S27 = 1 otherwise 0) with our exp. (Add? = true)
  //   If we were adding then it was Overflow otherwise underflow
  //   If there is no set bit in significand then output is 0 so carry doesnt matter then.
  //   Converts normal significand
  //   If 26th or 27th bit is set we dont left shift significant 
  //   So if any of them is set we make shift amount 0
endmodule

module ROUNDER (
  input  [24:0] S,
  input  [8:0] Exponent,
  output [21:0] R,
  output [8:0] RoundedExponent,
  output RoundingOverflow
);

  wire adder_1_cout, adder_2_cout, n7408_1_p3, n7432_1_p3, n7432_1_p6;
  wire [8:0] bit_extender_2_out;
  wire [21:0] bit_extender_1_out;

  // _7432 7432_1: pin names not known; wires that end beside it: S[1], S[0], n7432_1_p3, S[3], n7432_1_p3, n7432_1_p6
  assign bit_extender_1_out = {{21{1'b0}}, 1'b0};  // Bit_Extender bit_extender_1
  assign bit_extender_2_out = {{8{1'b0}}, 1'b0};  // Bit_Extender bit_extender_2
  Adder #(.width(22)) adder_1 (.a(S[24:3]), .b(bit_extender_1_out), .out(R), .cin(n7408_1_p3), .cout(adder_1_cout));
  Adder #(.width(9)) adder_2 (
    .a(Exponent), .b(bit_extender_2_out), .out(RoundedExponent), .cin(adder_1_cout), .cout(adder_2_cout));
  // _7408 7408_1: pin names not known; wires that end beside it: S[2], n7432_1_p6, n7408_1_p3
  Error_Detector error_detector_1 (
    .Exponent(RoundedExponent), .Carry_borrow(adder_2_cout), .Overflow_Underflow(RoundingOverflow));

  // Other names for the same wires on the sheet: Sticky = S[0]; Round = S[1]; Guard = S[2]; S0 = S[3];
  //   S_t[21:0] = S[24:3]

  // Notes on the sheet:
  //   Overflow can also occur when rounding values
  //   Add one if G AND (R + S + S0) = 1
endmodule

module ASU (
  input  B_Cin,
  input  Add,
  input  [26:0] A,
  input  [26:0] B,
  output [27:0] Y
);

  wire bout, cout;
  wire [26:0] Add_t, Sub;

  // Probe on A
  // Probe on B
  Adder #(.width(27)) adder_1 (.a(A), .b(B), .out(Add_t), .cin(B_Cin), .cout(cout));
  Subtractor #(.width(27)) subtractor_1 (.a(A), .b(B), .out(Sub), .bin(B_Cin), .bout(bout));
  // _74157 74157_1: pin names not known; wires that end beside it: Add, bout, cout, Y[27], 1'b0
  Multiplexer #(.width(27), .enable("false")) multiplexer_1 (.in0(Sub), .in1(Add_t), .out(Y[26:0]), .sel(Add));
  // Probe on Y
endmodule

module ABS (
  input  [27:0] A,
  output [26:0] ABS
);

  wire [26:0] _1_s_Comp, bit_extender_1_out;

  // _7486 7486_1: pin names not known; wires that end beside it: A[0], A[27], _1_s_Comp[0], A[1], A[27], _1_s_Comp[1], A[27], A[3], _1_s_Comp[3], A[27], A[2], _1_s_Comp[2]
  // _7486 7486_2: pin names not known; wires that end beside it: A[16], A[27], _1_s_Comp[16], A[17], A[27], _1_s_Comp[17], A[27], A[19], _1_s_Comp[19], A[27], A[18], _1_s_Comp[18]
  // Probe on A
  // _7486 7486_3: pin names not known; wires that end beside it: A[4], A[27], _1_s_Comp[4], A[5], A[27], _1_s_Comp[5], A[27], A[7], _1_s_Comp[7], A[27], A[6], _1_s_Comp[6]
  // _7486 7486_4: pin names not known; wires that end beside it: A[20], A[27], _1_s_Comp[20], A[21], A[27], _1_s_Comp[21], A[27], A[23], _1_s_Comp[23], A[27], A[22], _1_s_Comp[22]
  // _7486 7486_5: pin names not known; wires that end beside it: A[8], A[27], _1_s_Comp[8], A[9], A[27], _1_s_Comp[9], A[27], A[11], _1_s_Comp[11], A[27], A[10], _1_s_Comp[10]
  // _7486 7486_6: pin names not known; wires that end beside it: A[24], A[27], _1_s_Comp[24], A[25], A[27], _1_s_Comp[25], A[27], A[27], A[26], _1_s_Comp[26]
  // _7486 7486_7: pin names not known; wires that end beside it: A[12], A[27], _1_s_Comp[12], A[13], A[27], _1_s_Comp[13], A[27], A[15], _1_s_Comp[15], A[27], A[14], _1_s_Comp[14]
  assign bit_extender_1_out = {{26{1'b0}}, 1'b0};  // Bit_Extender bit_extender_1
  Adder #(.width(27)) adder_1 (.a(_1_s_Comp), .b(bit_extender_1_out), .out(ABS), .cin(A[27]));  // open: cout
  // Probe on ABS

  // Other names for the same wires on the sheet: Y0 = _1_s_Comp[0]; Y1 = _1_s_Comp[1]; Y2 = _1_s_Comp[2];
  //   Y3 = _1_s_Comp[3]; Y4 = _1_s_Comp[4]; Y5 = _1_s_Comp[5]; Y6 = _1_s_Comp[6]; Y7 = _1_s_Comp[7];
  //   Y8 = _1_s_Comp[8]; Y9 = _1_s_Comp[9]; Y10 = _1_s_Comp[10]; Y11 = _1_s_Comp[11]; Y12 = _1_s_Comp[12];
  //   Y13 = _1_s_Comp[13]; Y14 = _1_s_Comp[14]; Y15 = _1_s_Comp[15]; Y16 = _1_s_Comp[16]; Y17 = _1_s_Comp[17];
  //   Y18 = _1_s_Comp[18]; Y19 = _1_s_Comp[19]; Y20 = _1_s_Comp[20]; Y21 = _1_s_Comp[21]; Y22 = _1_s_Comp[22];
  //   Y23 = _1_s_Comp[23]; Y24 = _1_s_Comp[24]; Y25 = _1_s_Comp[25]; Y26 = _1_s_Comp[26]; Sign = A[27]
endmodule

module Flags_Checker (
  input  [21:0] Fraction,
  input  [8:0] Exponent,
  output ZERO,
  output DE_NORM,
  output INF,
  output NaN,
  output Floating_Point_Number
);

  wire not_1_out, not_2_out, not_3_out, zero_checker_1_iszero, zero_checker_2_iszero, zero_checker_3_iszero;
  wire [31:0] bit_extender_1_out, bit_extender_2_out, bit_extender_3_out, n32_bit_not_1_out_2;

  assign bit_extender_1_out = {{10{1'b0}}, Fraction};  // Bit_Extender bit_extender_1
  assign bit_extender_2_out = {{23{1'b0}}, Exponent};  // Bit_Extender bit_extender_2
  assign bit_extender_3_out = {{23{1'b1}}, Exponent};  // Bit_Extender bit_extender_3
  Zero_Checker zero_checker_1 (.A(bit_extender_1_out), .IsZero(zero_checker_1_iszero), .IgnoreSignBit(1'b0));
  Zero_Checker zero_checker_2 (.A(bit_extender_2_out), .IsZero(zero_checker_2_iszero), .IgnoreSignBit(1'b0));
  _32_bit_not u_32_bit_not_1 (.In(bit_extender_3_out), .out_2(n32_bit_not_1_out_2));
  Zero_Checker zero_checker_3 (.A(n32_bit_not_1_out_2), .IsZero(zero_checker_3_iszero), .IgnoreSignBit(1'b0));
  not not_1 (not_1_out, zero_checker_1_iszero);
  not not_2 (not_2_out, zero_checker_3_iszero);
  not not_3 (not_3_out, zero_checker_2_iszero);
  and and_1 (ZERO, zero_checker_1_iszero, zero_checker_2_iszero);
  and and_2 (DE_NORM, zero_checker_2_iszero, not_1_out);
  and and_3 (INF, zero_checker_1_iszero, zero_checker_3_iszero);
  and and_4 (NaN, zero_checker_3_iszero, not_1_out);
  and and_5 (Floating_Point_Number, not_2_out, not_3_out);

  // Notes on the sheet:
  //   Fraction and Exponent both all zeros
  //   Exponent all zero and fraction non-zero
  //   Exponent all one and fraction non zero
endmodule

module Zero_Checker (
  input  [31:0] A,
  input  IgnoreSignBit,
  output IsZero
);

  wire A31_NEW, n7432_1_p3, n7432_1_p6, n7432_1_p8, n7432_1_p9, n7432_2_p1, n7432_2_p3, n7432_2_p6,
       n7432_2_p8, n7432_2_p9, n7432_3_p3, n7432_3_p6, n7432_3_p8, n7432_3_p9, n7432_4_p3, n7432_4_p6,
       n7432_4_p8, n7432_4_p9, n7432_5_p3, n7432_5_p6, n7432_5_p8, n7432_5_p9, n7432_6_p3, n7432_6_p6,
       n7432_6_p8, n7432_6_p9, n7432_7_p3, n7432_7_p6, n7432_7_p8, n7432_8_p3, n7432_8_p6, n7432_8_p9,
       not_1_out;

  // _7432 7432_1: pin names not known; wires that end beside it: A[0], A[1], n7432_1_p3, n7432_1_p3, A[2], n7432_1_p6, A[3], n7432_1_p8, n7432_1_p9, A[4], n7432_1_p6, n7432_1_p8
  // _7432 7432_2: pin names not known; wires that end beside it: n7432_2_p1, A[17], n7432_2_p3, n7432_2_p3, A[18], n7432_2_p6, A[19], n7432_2_p8, n7432_2_p9, A[20], n7432_2_p6, n7432_2_p8
  // _7432 7432_3: pin names not known; wires that end beside it: n7432_1_p9, A[5], n7432_3_p3, n7432_3_p3, A[6], n7432_3_p6, A[7], n7432_3_p8, n7432_3_p9, A[8], n7432_3_p6, n7432_3_p8
  // _7432 7432_4: pin names not known; wires that end beside it: n7432_2_p9, A[21], n7432_4_p3, n7432_4_p3, A[22], n7432_4_p6, A[23], n7432_4_p8, n7432_4_p9, A[24], n7432_4_p6, n7432_4_p8
  // _7432 7432_5: pin names not known; wires that end beside it: n7432_3_p9, A[9], n7432_5_p3, n7432_5_p3, A[10], n7432_5_p6, A[11], n7432_5_p8, n7432_5_p9, A[12], n7432_5_p6, n7432_5_p8
  // _7432 7432_6: pin names not known; wires that end beside it: n7432_4_p9, A[25], n7432_6_p3, n7432_6_p3, A[26], n7432_6_p6, A[27], n7432_6_p8, n7432_6_p9, A[28], n7432_6_p6, n7432_6_p8
  and and_1 (A31_NEW, A[31], not_1_out);
  not not_1 (not_1_out, IgnoreSignBit);
  // _7432 7432_7: pin names not known; wires that end beside it: n7432_5_p9, A[13], n7432_7_p3, n7432_7_p3, A[14], n7432_7_p6, A[15], n7432_7_p8, n7432_2_p1, A[16], n7432_7_p6, n7432_7_p8
  // _7432 7432_8: pin names not known; wires that end beside it: n7432_6_p9, A[29], n7432_8_p3, n7432_8_p3, A[30], n7432_8_p6, A31_NEW, n7432_8_p6, n7432_8_p9
  not not_2 (IsZero, n7432_8_p9);

  // Notes on the sheet:
  //   Sign bit is not included, so -0 and +0 is not different.
endmodule

module Error_Detector (
  input  [8:0] Exponent,
  input  Carry_borrow,
  output Overflow_Underflow
);

  Subtractor #(.width(10)) subtractor_1 (
    .a(10'h1fe), .b({Carry_borrow, Exponent}), .bout(Overflow_Underflow));  // open: out, bin

  // Notes on the sheet:
  //   Checks if the exponent is larger than 11111110 which means overflow 
  //   0 111111110 - first zero for padding 
endmodule

// 8x3 ENC
module _8_bit_priority_encoder (
  input  _1__I4,
  input  _16__Vcc,
  input  _2__I5,
  input  _3__I6,
  input  _4__I7,
  input  _13__I3,
  input  _5__EI,
  input  _12__I2,
  input  _11__I1,
  input  _10__I0,
  input  _8__GND,
  output _15__EO,
  output _16__GS,
  output _6__A2,
  output _7__A1,
  output _9__A0
);

  wire not_1_out, not_2_out, not_3_out, not_4_out, not_5_out, not_6_out, not_7_out, not_8_out, not_9_out,
       not_10_out, not_11_out, not_12_out, priority_encoder_1_en_out, priority_encoder_1_gs;
  wire [2:0] priority_encoder_1_out;

  or or_1 (_16__GS, priority_encoder_1_en_out, _5__EI);
  not not_1 (not_1_out, _10__I0);
  not not_2 (not_2_out, _11__I1);
  not not_3 (not_3_out, _12__I2);
  Priority_Encoder #(.disabled(0)) priority_encoder_1 (
    .in0(not_1_out), .in1(not_2_out), .in2(not_3_out), .in3(not_4_out), .in4(not_5_out), .in5(not_6_out),
    .in6(not_7_out), .in7(not_8_out), .out(priority_encoder_1_out), .en_in(not_9_out),
    .gs(priority_encoder_1_gs), .en_out(priority_encoder_1_en_out));
  not not_4 (not_4_out, _13__I3);
  not not_5 (not_5_out, _1__I4);
  not not_6 (not_6_out, _2__I5);
  not not_7 (not_7_out, _3__I6);
  not not_8 (not_8_out, _4__I7);
  not not_9 (not_9_out, _5__EI);
  or or_2 (_15__EO, priority_encoder_1_gs, _5__EI);
  not not_10 (not_10_out, priority_encoder_1_out[0]);
  not not_11 (not_11_out, priority_encoder_1_out[1]);
  not not_12 (not_12_out, priority_encoder_1_out[2]);
  or or_3 (_9__A0, not_10_out, _16__GS);
  or or_4 (_7__A1, not_11_out, _16__GS);
  or or_5 (_6__A2, not_12_out, _16__GS);

  // Other names for the same wires on the sheet: A0 = _9__A0; A1 = _7__A1; A2 = _6__A2; E = _5__EI; EO = _15__EO;
  //   GS = _16__GS; I0 = _10__I0; I1 = _11__I1; I2 = _12__I2; I3 = _13__I3; I4 = _1__I4; I5 = _2__I5; I6 = _3__I6;
  //   I7 = _4__I7

  // Notes on the sheet:
  //   _16__Vcc: pull=up
  //   _8__GND: pull=down
  //   74148: 8-Line to 4-Line Priority Encoder
  //   [GS] GROUP SELECT bit represents validity of input bits (If no bit is 0 then GS is 1)
endmodule

// 16x4 ENC
module _16_bit_priority_encoder (
  input  [15:0] In,
  input  EI,
  output [3:0] Out,
  output EO,
  output GS
);

  wire A0_0, A0_1, A1_0, A1_1, A2_0, A2_1, GS_0, n8_bit_priority_encoder_1__15__eo;

  _8_bit_priority_encoder u_8_bit_priority_encoder_1 (
    ._1__I4(In[12]), ._2__I5(In[13]), ._3__I6(In[14]), ._4__I7(In[15]), ._5__EI(EI), ._6__A2(A2_1),
    ._7__A1(A1_1), ._15__EO(n8_bit_priority_encoder_1__15__eo), ._16__GS(Out[3]), ._13__I3(In[11]),
    ._12__I2(In[10]), ._11__I1(In[9]), ._10__I0(In[8]), ._9__A0(A0_1));  // open: _8__GND, _16__Vcc
  _8_bit_priority_encoder u_8_bit_priority_encoder_2 (
    ._1__I4(In[4]), ._2__I5(In[5]), ._3__I6(In[6]), ._4__I7(In[7]),
    ._5__EI(n8_bit_priority_encoder_1__15__eo), ._6__A2(A2_0), ._7__A1(A1_0), ._15__EO(EO), ._16__GS(GS_0),
    ._13__I3(In[3]), ._12__I2(In[2]), ._11__I1(In[1]), ._10__I0(In[0]), ._9__A0(A0_0));  // open: _8__GND, _16__Vcc
  // _7408 7408_1: pin names not known; wires that end beside it: A0_0, A0_1, Out[0], A1_0, A1_1, Out[1], A2_0, A2_1, Out[2], Out[3], GS_0, GS

  // Other names for the same wires on the sheet: I0 = In[0]; I1 = In[1]; I2 = In[2]; I3 = In[3]; I4 = In[4];
  //   I5 = In[5]; I6 = In[6]; I7 = In[7]; I8 = In[8]; I9 = In[9]; I10 = In[10]; I11 = In[11]; I12 = In[12];
  //   I13 = In[13]; I14 = In[14]; I15 = In[15]; A0 = Out[0]; A1 = Out[1]; A2 = Out[2]; A3 = Out[3]; GS_1 = Out[3]

  // Notes on the sheet:
  //   INPUT PINS
  //   OUTPUT PINS
endmodule

// 32x5 ENC
module _32_bit_priority_encoder (
  input  [31:0] in_1,
  input  in_2,
  output [4:0] Out,
  output EO,
  output GS
);

  wire A0_0, A0_1, A1_0, A1_1, A2_0, A2_1, A3_0, A3_1, GS_0, n16_bit_priority_encoder_1_eo;

  _16_bit_priority_encoder u_16_bit_priority_encoder_1 (
    .In(in_1[31:16]), .EI(in_2), .Out({A3_1, A2_1, A1_1, A0_1}), .EO(n16_bit_priority_encoder_1_eo),
    .GS(Out[4]));
  _16_bit_priority_encoder u_16_bit_priority_encoder_2 (
    .In(in_1[15:0]), .EI(n16_bit_priority_encoder_1_eo), .Out({A3_0, A2_0, A1_0, A0_0}), .EO(EO), .GS(GS_0));
  // _7408 7408_1: pin names not known; wires that end beside it: A0_0, A0_1, Out[0], A1_0, A1_1, Out[1], A2_0, A2_1, Out[2], A3_0, A3_1
  // _7408 7408_2: pin names not known; wires that end beside it: Out[4], GS_0, GS, Out[3]

  // Other names for the same wires on the sheet: EI = in_2; I0[15:0] = in_1[15:0]; I1[15:0] = in_1[31:16];
  //   O0[3:0] = {A3_0, A2_0, A1_0, A0_0}; O1[3:0] = {A3_1, A2_1, A1_1, A0_1}; A0 = Out[0]; A1 = Out[1]; A2 = Out[2];
  //   A3 = Out[3]; A4 = Out[4]; GS_1 = Out[4]

  // Notes on the sheet:
  //   OUTPUT PINS
  //   INPUT PINS
endmodule

// 32 NOT
module _32_bit_not (
  input  [31:0] In,
  output [31:0] out_2
);

  // _7404 7404_1: pin names not known; wires that end beside it: In[0], out_2[0], In[1], out_2[1], In[2], In[3], out_2[3], In[4], out_2[4]
  // _7404 7404_2: pin names not known; wires that end beside it: out_2[2], In[6], out_2[6], In[7], out_2[7], In[8], In[5], out_2[5], In[9], out_2[9], In[10], out_2[10]
  // _7404 7404_3: pin names not known; wires that end beside it: out_2[8], In[12], out_2[12], In[13], out_2[13], In[14], In[11], out_2[11], In[15], out_2[15], In[16], out_2[16]
  // _7404 7404_4: pin names not known; wires that end beside it: out_2[14], In[18], out_2[18], In[19], out_2[19], In[20], In[17], out_2[17], In[21], out_2[21], In[22], out_2[22]
  // _7404 7404_5: pin names not known; wires that end beside it: out_2[20], In[24], out_2[24], In[25], out_2[25], In[26], In[23], out_2[23], In[27], out_2[27], In[28], out_2[28]
  // _7404 7404_6: pin names not known; wires that end beside it: out_2[26], In[30], out_2[30], In[31], out_2[31], In[29], out_2[29]

  // Other names for the same wires on the sheet: I0 = In[0]; I1 = In[1]; I2 = In[2]; I3 = In[3]; I4 = In[4];
  //   I5 = In[5]; I6 = In[6]; I7 = In[7]; I8 = In[8]; I9 = In[9]; I10 = In[10]; I11 = In[11]; I12 = In[12];
  //   I13 = In[13]; I14 = In[14]; I15 = In[15]; I16 = In[16]; I17 = In[17]; I18 = In[18]; I19 = In[19]; I20 = In[20];
  //   I21 = In[21]; I22 = In[22]; I23 = In[23]; I24 = In[24]; I25 = In[25]; I26 = In[26]; I27 = In[27]; I28 = In[28];
  //   I29 = In[29]; I30 = In[30]; I31 = In[31]; I0_prime = out_2[0]; I1_prime = out_2[1]; I2_prime = out_2[2];
  //   I3_prime = out_2[3]; I4_prime = out_2[4]; I5_prime = out_2[5]; I6_prime = out_2[6]; I7_prime = out_2[7];
  //   I8_prime = out_2[8]; I9_prime = out_2[9]; I10_prime = out_2[10]; I11_prime = out_2[11]; I12_prime = out_2[12];
  //   I13_prime = out_2[13]; I14_prime = out_2[14]; I15_prime = out_2[15]; I16_prime = out_2[16];
  //   I17_prime = out_2[17]; I18_prime = out_2[18]; I19_prime = out_2[19]; I20_prime = out_2[20];
  //   I21_prime = out_2[21]; I22_prime = out_2[22]; I23_prime = out_2[23]; I24_prime = out_2[24];
  //   I25_prime = out_2[25]; I26_prime = out_2[26]; I27_prime = out_2[27]; I28_prime = out_2[28];
  //   I29_prime = out_2[29]; I30_prime = out_2[30]; I31_prime = out_2[31]

  // Notes on the sheet:
  //   INPUT PINS
  //   OUTPUT PINS
endmodule

// 32x5 HIGH ENC
module _32_bit_high_priority_encoder (
  input  _1_based_indexing,
  input  [31:0] In,
  input  EI,
  output [4:0] Out
);

  wire EO, GS;
  wire [4:0] n32_bit_priority_encoder_1_out;
  wire [31:0] n32_bit_not_1_out_2;

  _32_bit_not u_32_bit_not_1 (.In(In), .out_2(n32_bit_not_1_out_2));
  _32_bit_priority_encoder u_32_bit_priority_encoder_1 (
    .in_1(n32_bit_not_1_out_2), .in_2(EI), .Out(n32_bit_priority_encoder_1_out), .EO(EO), .GS(GS));
  Adder #(.width(5)) adder_1 (
    .a(n32_bit_priority_encoder_1_out), .b({5{1'b0}}), .out(Out), .cin(_1_based_indexing));  // open: cout

  // Notes on the sheet:
  //   Convert to ACTIVE LOW
  //   If one based indexing add 1 
  //   1-based indexing is needed when left shifting bits.
  //   Though position of first 1 is 0 we need to shift it once so we take 1-based indexing
endmodule

module _1_bit_RS (
  input  [26:0] S,
  input  Enable,
  output [26:0] out
);

  wire [26:0] Shifted;
  wire [31:0] bit_extender_1_out, bit_extender_2_out;
  wire [31:27] n32_bit_mux_1_out;

  assign bit_extender_1_out = {{5{1'b0}}, S};  // Bit_Extender bit_extender_1
  assign bit_extender_2_out = {{5{1'b0}}, Shifted};  // Bit_Extender bit_extender_2
  Shifter #(.width(27), .shift("lr")) shifter_1 (.in(S), .\dist (5'b00001), .out(Shifted));
  _32_bit_MUX u_32_bit_mux_1 (
    .A(bit_extender_1_out), .B(bit_extender_2_out), .Out({n32_bit_mux_1_out, out}), .S(Enable));
endmodule

module _2_bit_RS (
  input  [26:0] S,
  input  Enable,
  output [26:0] out
);

  wire [26:0] Shifted;
  wire [31:0] bit_extender_1_out, bit_extender_2_out;
  wire [31:27] n32_bit_mux_1_out;

  assign bit_extender_1_out = {{5{1'b0}}, S};  // Bit_Extender bit_extender_1
  assign bit_extender_2_out = {{5{1'b0}}, Shifted};  // Bit_Extender bit_extender_2
  Shifter #(.width(27), .shift("lr")) shifter_1 (.in(S), .\dist (5'b00010), .out(Shifted));
  _32_bit_MUX u_32_bit_mux_1 (
    .A(bit_extender_1_out), .B(bit_extender_2_out), .Out({n32_bit_mux_1_out, out}), .S(Enable));
endmodule

module _4_bit_RS (
  input  [26:0] S,
  input  Enable,
  output [26:0] out
);

  wire [26:0] Shifted;
  wire [31:0] bit_extender_1_out, bit_extender_2_out;
  wire [31:27] n32_bit_mux_1_out;

  assign bit_extender_1_out = {{5{1'b0}}, S};  // Bit_Extender bit_extender_1
  assign bit_extender_2_out = {{5{1'b0}}, Shifted};  // Bit_Extender bit_extender_2
  Shifter #(.width(27), .shift("lr")) shifter_1 (.in(S), .\dist (5'b00100), .out(Shifted));
  _32_bit_MUX u_32_bit_mux_1 (
    .A(bit_extender_1_out), .B(bit_extender_2_out), .Out({n32_bit_mux_1_out, out}), .S(Enable));
endmodule

module _8_bit_RS (
  input  [26:0] S,
  input  Enable,
  output [26:0] out
);

  wire [26:0] Shifted;
  wire [31:0] bit_extender_1_out, bit_extender_2_out;
  wire [31:27] n32_bit_mux_1_out;

  assign bit_extender_1_out = {{5{1'b0}}, S};  // Bit_Extender bit_extender_1
  assign bit_extender_2_out = {{5{1'b0}}, Shifted};  // Bit_Extender bit_extender_2
  Shifter #(.width(27), .shift("lr")) shifter_1 (.in(S), .\dist (5'b01000), .out(Shifted));
  _32_bit_MUX u_32_bit_mux_1 (
    .A(bit_extender_1_out), .B(bit_extender_2_out), .Out({n32_bit_mux_1_out, out}), .S(Enable));
endmodule

module _16_bit_RS (
  input  [26:0] S,
  input  Enable,
  output [26:0] out
);

  wire [26:0] Shifted;
  wire [31:0] bit_extender_1_out, bit_extender_2_out;
  wire [31:27] n32_bit_mux_1_out;

  assign bit_extender_1_out = {{5{1'b0}}, S};  // Bit_Extender bit_extender_1
  assign bit_extender_2_out = {{5{1'b0}}, Shifted};  // Bit_Extender bit_extender_2
  Shifter #(.width(27), .shift("lr")) shifter_1 (.in(S), .\dist (5'b10000), .out(Shifted));
  _32_bit_MUX u_32_bit_mux_1 (
    .A(bit_extender_1_out), .B(bit_extender_2_out), .Out({n32_bit_mux_1_out, out}), .S(Enable));
endmodule

module Right_Shifter (
  input  [4:0] E,
  input  [26:0] A,
  output [26:0] Y
);

  wire [26:0] n2_bit_rs_1_out, n4_bit_rs_1_out, n8_bit_rs_1_out, n16_bit_rs_1_out;

  _16_bit_RS u_16_bit_rs_1 (.S(A), .Enable(E[4]), .out(n16_bit_rs_1_out));
  _8_bit_RS u_8_bit_rs_1 (.S(n16_bit_rs_1_out), .Enable(E[3]), .out(n8_bit_rs_1_out));
  _4_bit_RS u_4_bit_rs_1 (.S(n8_bit_rs_1_out), .Enable(E[2]), .out(n4_bit_rs_1_out));
  _2_bit_RS u_2_bit_rs_1 (.S(n4_bit_rs_1_out), .Enable(E[1]), .out(n2_bit_rs_1_out));
  _1_bit_RS u_1_bit_rs_1 (.S(n2_bit_rs_1_out), .Enable(E[0]), .out(Y));
endmodule

module Right_Shift_Adapter (
  input  [8:0] S,
  output [4:0] E
);

  wire n7432_1_p2;

  // Probe on S
  // _7432 7432_1: pin names not known; wires that end beside it: S[4], n7432_1_p2, E[4], S[3], n7432_1_p2, E[3], n7432_1_p2, S[1], E[1], n7432_1_p2, S[2], E[2]
  Subtractor #(.width(9)) subtractor_1 (.a(9'h1b), .b(S), .bin(1'b0), .bout(n7432_1_p2));  // open: out
  // _7432 7432_2: pin names not known; wires that end beside it: S[0], n7432_1_p2, E[0]

  // Notes on the sheet:
  //   Decimal : 27
  //   ORs with the borrow out (1 if E > 27) 
  //   Check if the exponent is greater than 27
  //   If exponent is greater than 27 then turn on all 
  //   shift bits to make the signifant fully zero
  //   as we can shift at most 27 bits
endmodule

module _9_bit_MUX (
  input  [8:0] A,
  input  [8:0] B,
  input  S,
  output [8:0] Y
);

  wire [31:0] bit_extender_1_out, bit_extender_2_out, n32_bit_mux_1_out;

  assign bit_extender_1_out = {{23{1'b0}}, A};  // Bit_Extender bit_extender_1
  assign bit_extender_2_out = {{23{1'b0}}, B};  // Bit_Extender bit_extender_2
  _32_bit_MUX u_32_bit_mux_1 (.A(bit_extender_1_out), .B(bit_extender_2_out), .Out(n32_bit_mux_1_out), .S(S));
  Bit_Extender #(.in_width(32), .out_width(9)) bit_extender_3 (.in(n32_bit_mux_1_out), .out(Y));
endmodule

module _32_bit_MUX (
  input  [31:0] A,
  input  [31:0] B,
  input  S,
  output [31:0] Out
);

  // _74157 74157_1: pin names not known; wires that end beside it: S, A[0], B[0], Out[0], A[1], B[1], Out[1], 1'b0, A[3], B[3], Out[3], A[2], B[2], Out[2]
  // _74157 74157_2: pin names not known; wires that end beside it: S, A[8], B[8], Out[8], A[9], B[9], Out[9], 1'b0, A[11], B[11], Out[11], A[10], B[10], Out[10]
  // _74157 74157_3: pin names not known; wires that end beside it: S, A[16], B[16], Out[16], A[17], B[17], Out[17], 1'b0, A[19], B[19], Out[19], A[18], B[18], Out[18]
  // _74157 74157_4: pin names not known; wires that end beside it: S, A[24], B[24], Out[24], A[25], B[25], Out[25], 1'b0, A[27], B[27], Out[27], A[26], B[26], Out[26]
  // _74157 74157_5: pin names not known; wires that end beside it: S, A[4], B[4], Out[4], A[5], B[5], Out[5], 1'b0, A[7], B[7], Out[7], A[6], B[6], Out[6]
  // _74157 74157_6: pin names not known; wires that end beside it: S, A[12], B[12], Out[12], A[13], B[13], Out[13], 1'b0, A[15], B[15], Out[15], A[14], B[14], Out[14]
  // _74157 74157_7: pin names not known; wires that end beside it: S, A[20], B[20], Out[20], A[21], B[21], Out[21], 1'b0, A[23], B[23], Out[23], A[22], B[22], Out[22]
  // _74157 74157_8: pin names not known; wires that end beside it: S, A[28], B[28], Out[28], A[29], B[29], Out[29], 1'b0, A[31], B[31], Out[31], A[30], B[30], Out[30]

  // Other names for the same wires on the sheet: Y0 = Out[0]; Y1 = Out[1]; Y2 = Out[2]; Y3 = Out[3]; Y4 = Out[4];
  //   Y5 = Out[5]; Y6 = Out[6]; Y7 = Out[7]; Y8 = Out[8]; Y9 = Out[9]; Y10 = Out[10]; Y11 = Out[11]; Y12 = Out[12];
  //   Y13 = Out[13]; Y14 = Out[14]; Y15 = Out[15]; Y16 = Out[16]; Y17 = Out[17]; Y18 = Out[18]; Y19 = Out[19];
  //   Y20 = Out[20]; Y21 = Out[21]; Y22 = Out[22]; Y23 = Out[23]; Y24 = Out[24]; Y25 = Out[25]; Y26 = Out[26];
  //   Y27 = Out[27]; Y28 = Out[28]; Y29 = Out[29]; Y30 = Out[30]; Y31 = Out[31]

  // Notes on the sheet:
  //   INPUT PINS
  //   OUTPUT PINS
endmodule

module _1_bit_LS (
  input  [26:0] S,
  input  Enable,
  output [26:0] out_3
);

  wire [26:0] Shifted;
  wire [31:0] bit_extender_1_out, bit_extender_2_out;
  wire [31:27] n32_bit_mux_1_out;

  assign bit_extender_1_out = {{5{1'b0}}, S};  // Bit_Extender bit_extender_1
  assign bit_extender_2_out = {{5{1'b0}}, Shifted};  // Bit_Extender bit_extender_2
  Shifter #(.width(27)) shifter_1 (.in(S), .\dist (5'b00001), .out(Shifted));
  _32_bit_MUX u_32_bit_mux_1 (
    .A(bit_extender_1_out), .B(bit_extender_2_out), .Out({n32_bit_mux_1_out, out_3}), .S(Enable));
endmodule

module _2_bit_LS (
  input  [26:0] S,
  input  Enable,
  output [26:0] out_3
);

  wire [26:0] Shifted;
  wire [31:0] bit_extender_1_out, bit_extender_2_out;
  wire [31:27] n32_bit_mux_1_out;

  assign bit_extender_1_out = {{5{1'b0}}, S};  // Bit_Extender bit_extender_1
  assign bit_extender_2_out = {{5{1'b0}}, Shifted};  // Bit_Extender bit_extender_2
  Shifter #(.width(27)) shifter_1 (.in(S), .\dist (5'b00010), .out(Shifted));
  _32_bit_MUX u_32_bit_mux_1 (
    .A(bit_extender_1_out), .B(bit_extender_2_out), .Out({n32_bit_mux_1_out, out_3}), .S(Enable));
endmodule

module _4_bit_LS (
  input  [26:0] S,
  input  Enable,
  output [26:0] out_3
);

  wire [26:0] Shifted;
  wire [31:0] bit_extender_1_out, bit_extender_2_out;
  wire [31:27] n32_bit_mux_1_out;

  assign bit_extender_1_out = {{5{1'b0}}, S};  // Bit_Extender bit_extender_1
  assign bit_extender_2_out = {{5{1'b0}}, Shifted};  // Bit_Extender bit_extender_2
  Shifter #(.width(27)) shifter_1 (.in(S), .\dist (5'b00100), .out(Shifted));
  _32_bit_MUX u_32_bit_mux_1 (
    .A(bit_extender_1_out), .B(bit_extender_2_out), .Out({n32_bit_mux_1_out, out_3}), .S(Enable));
endmodule

module _8_bit_LS (
  input  [26:0] S,
  input  Enable,
  output [26:0] out_3
);

  wire [26:0] Shifted;
  wire [31:0] bit_extender_1_out, bit_extender_2_out;
  wire [31:27] n32_bit_mux_1_out;

  assign bit_extender_1_out = {{5{1'b0}}, S};  // Bit_Extender bit_extender_1
  assign bit_extender_2_out = {{5{1'b0}}, Shifted};  // Bit_Extender bit_extender_2
  Shifter #(.width(27)) shifter_1 (.in(S), .\dist (5'b01000), .out(Shifted));
  _32_bit_MUX u_32_bit_mux_1 (
    .A(bit_extender_1_out), .B(bit_extender_2_out), .Out({n32_bit_mux_1_out, out_3}), .S(Enable));
endmodule

module _16_bit_LS (
  input  [26:0] S,
  input  Enable,
  output [26:0] out_3
);

  wire [26:0] Shifted;
  wire [31:0] bit_extender_1_out, bit_extender_2_out;
  wire [31:27] n32_bit_mux_1_out;

  assign bit_extender_1_out = {{5{1'b0}}, S};  // Bit_Extender bit_extender_1
  assign bit_extender_2_out = {{5{1'b0}}, Shifted};  // Bit_Extender bit_extender_2
  Shifter #(.width(27)) shifter_1 (.in(S), .\dist (5'b10000), .out(Shifted));
  _32_bit_MUX u_32_bit_mux_1 (
    .A(bit_extender_1_out), .B(bit_extender_2_out), .Out({n32_bit_mux_1_out, out_3}), .S(Enable));
endmodule

module Left_Shifter (
  input  [4:0] E,
  input  [26:0] A,
  output [26:0] Y
);

  wire [26:0] n2_bit_ls_1_out_3, n4_bit_ls_1_out_3, n8_bit_ls_1_out_3, n16_bit_ls_1_out_3;

  _16_bit_LS u_16_bit_ls_1 (.S(A), .Enable(E[4]), .out_3(n16_bit_ls_1_out_3));
  _8_bit_LS u_8_bit_ls_1 (.S(n16_bit_ls_1_out_3), .Enable(E[3]), .out_3(n8_bit_ls_1_out_3));
  _4_bit_LS u_4_bit_ls_1 (.S(n8_bit_ls_1_out_3), .Enable(E[2]), .out_3(n4_bit_ls_1_out_3));
  _2_bit_LS u_2_bit_ls_1 (.S(n4_bit_ls_1_out_3), .out_3(n2_bit_ls_1_out_3), .Enable(E[1]));
  _1_bit_LS u_1_bit_ls_1 (.S(n2_bit_ls_1_out_3), .out_3(Y), .Enable(E[0]));
endmodule
